# Fritzing sketch _2door-1pir-sample (saved by Fritzing 0.9.3b)
breadboards: 1

parts:
  U1 = ESP8266 WiFi Module [part_number=ESP8266]
  PIR1 = PIR sensor
  S1 = Reed switch [package=THT]
  S2 = Reed switch [package=THT]

nets:
  VCC: U1.VCC, PIR1.VDD
  N1: U1.GND, PIR1.SIG, S1.pin_2, S2.pin_2
  N2: U1.GPIO_4, PIR1.GND
  N3: U1.GPIO_5, S1.pin_1
  N4: U1.GPIO_12, S2.pin_1
