# Fritzing sketch simple_toiletevolution (saved by Fritzing 0.9.3b)

parts:
  U1 = ESP8266 WiFi Module [part_number=ESP8266]
  PIR1 = PIR sensor

nets:
  VCC: U1.VCC, PIR1.VDD
  N1: U1.GND, PIR1.SIG
  N2: U1.GPIO_4, PIR1.GND
